# Fritzing sketch wiring-diagram (saved by Fritzing 0.9.2b)
breadboards: 3

parts:
  M1 = DC Motor  # not connected
  M2 = DC Motor  # not connected
  Componente1 = Arduino Uno (Rev3)
  Componente2 = Motor Driver 1A Dual TB6612FNG  # not connected
  LED1 = smd LED [color="Red (633nm)" package="0805 [SMD]"]
  R1 = Resistor [tolerance=±5% resistance=220 package=THT]

nets:
  N1: Componente1.D13/SCK, R1.Pin_0
  N2: Componente1.GND, LED1.cathode
  N3: LED1.anode, R1.Pin_1

notes:
  Battery 14.6V
  PS2 Controller
  -------------------
  1 Acknoledge
  2 N/A
  3 Clock
  4 Attention
  5 Power 3.3V
  6 Ground
  7 N/A
  8 Command
  9 Data
  Left motor
  Right motor
  Led Hull MG
